// Logisim project PROJECT.circ as structural Verilog
module main (
);

  wire DOWN_out, LEFT_out, RESET_out, RIGHT_out, TACTS, UP_out;

  Clock clock_1 (.out(TACTS));
  Button UP (.out(UP_out));
  Button DOWN (.out(DOWN_out));
  Button LEFT (.out(LEFT_out));
  Button RIGHT (.out(RIGHT_out));
  Button RESET (.out(RESET_out));
  BTN_INPUT btn_input_1 (
    .in_1(TACTS), .in_2(UP_out), .in_3(DOWN_out), .in_4(LEFT_out), .in_5(RIGHT_out), .in_6(RESET_out));  // open: out_7, out_8, out_9, out_10, out_11
  PLAYER_POS player_pos_1 (
    .in_2(TACTS), .in_5(TACTS), .in_3(TACTS), .in_6(TACTS));  // open: NEW_X, NEW_Y, LOAD_X, RESET, LOAD_Y, out_10, out_12, out_11
endmodule

module BTN_INPUT (
  input  in_1,
  input  in_2,
  input  in_3,
  input  in_4,
  input  in_5,
  input  in_6,
  output out_7,
  output out_8,
  output out_9,
  output out_10,
  output out_11
);

  wire d_ff_1_q, d_ff_2_q, d_ff_3_q, d_ff_4_q, not_1_out, not_2_out, not_3_out, not_4_out;

  D_Flip_Flop d_ff_1 (.clk(in_1), .D(in_2), .Q(d_ff_1_q));  // open: Qn, preset, en, reset
  D_Flip_Flop d_ff_2 (.clk(in_1), .D(in_3), .Q(d_ff_2_q));  // open: Qn, preset, en, reset
  D_Flip_Flop d_ff_3 (.clk(in_1), .D(in_4), .Q(d_ff_3_q));  // open: Qn, preset, en, reset
  D_Flip_Flop d_ff_4 (.clk(in_1), .D(in_5), .Q(d_ff_4_q));  // open: Qn, preset, en, reset
  not not_1 (not_1_out, d_ff_1_q);
  not not_2 (not_2_out, d_ff_2_q);
  not not_3 (not_3_out, d_ff_3_q);
  not not_4 (not_4_out, d_ff_4_q);
  and and_1 (out_7, d_ff_1_q, not_1_out);
  and and_2 (out_8, d_ff_2_q, not_2_out);
  and and_3 (out_9, d_ff_3_q, not_3_out);
  and and_4 (out_10, d_ff_4_q, not_4_out);

  assign out_11 = in_6;
endmodule

module PLAYER_POS (
  input  [5:0] NEW_X,
  input  in_2,
  input  in_3,
  input  [5:0] NEW_Y,
  input  in_5,
  input  in_6,
  input  LOAD_X,
  input  RESET,
  input  LOAD_Y,
  output [5:0] out_10,
  output [11:0] out_11,
  output [5:0] out_12
);

  wire LOAD_X_OR_RESET, LOAD_Y_OR_RESET;
  wire [5:0] multiplexer_1_out, multiplexer_2_out;

  or or_1 (LOAD_X_OR_RESET, LOAD_X, RESET);
  or or_2 (LOAD_Y_OR_RESET, RESET, LOAD_Y);
  Multiplexer #(.width(6)) multiplexer_1 (
    .in0(NEW_X), .in1(6'b000010), .out(multiplexer_1_out), .sel(in_2));  // open: en
  Multiplexer #(.width(6)) multiplexer_2 (
    .in0(NEW_Y), .in1(6'b000010), .out(multiplexer_2_out), .sel(in_5));  // open: en
  Register #(.width(6)) POS_X (.D(multiplexer_1_out), .en(LOAD_X_OR_RESET), .Q(out_10), .clk(in_3));  // open: clr
  Register #(.width(6)) POS_Y (.D(multiplexer_2_out), .en(LOAD_Y_OR_RESET), .Q(out_11[11:6]), .clk(in_6));  // open: clr

  assign out_11[5:0] = out_10;
  assign out_12 = out_11[11:6];

  // Notes on the sheet:
  //   START_X
  //   START_Y
endmodule

module MAP_MEM (
  input  [11:0] in_1,
  input  [3:0] in_2,
  input  in_3
);

  RAM #(.addrWidth(12), .dataWidth(4)) ram_1 (.addr(in_1), .data(in_2), .clk(in_3));  // open: sel, ld, clr
  RAM #(.addrWidth(12), .dataWidth(4)) ram_2 ();  // open: addr, data, sel, clk, ld, clr
  Counter counter_1 ();  // open: load, D, count, Q, carry, clk, clr

  // Notes on the sheet:
  //   MAP_DATA_BACKUP
  //   MAP_DATA
endmodule

module MOVE_LOGIC (
  input  [5:0] in_1,
  input  [5:0] in_2,
  input  [5:0] in_3,
  input  [5:0] in_4,
  input  [5:0] in_5,
  input  [5:0] in_6,
  input  [5:0] in_7,
  input  [5:0] in_8
);

  wire comparator_1_eq, comparator_1_gt, comparator_1_lt, comparator_2_eq, comparator_2_gt, comparator_2_lt,
       comparator_3_eq, comparator_3_gt, comparator_3_lt, comparator_4_eq, comparator_4_gt, comparator_4_lt;
  wire [5:0] adder_1_out, adder_2_out, subtractor_1_out, subtractor_2_out;

  Adder #(.width(6)) adder_1 (.a(in_1), .b(6'b000001), .out(adder_1_out));  // open: cin, cout
  Adder #(.width(6)) adder_2 (.a(in_2), .b(6'b000001), .out(adder_2_out));  // open: cin, cout
  Subtractor #(.width(6)) subtractor_1 (.a(in_3), .b(6'b000001), .out(subtractor_1_out));  // open: bin, bout
  Subtractor #(.width(6)) subtractor_2 (.a(in_4), .b(6'b000001), .out(subtractor_2_out));  // open: bin, bout
  Comparator #(.width(6)) comparator_1 (
    .a(in_5), .b(6'b100011), .gt(comparator_1_gt), .eq(comparator_1_eq), .lt(comparator_1_lt));
  Comparator #(.width(6)) comparator_2 (
    .a(in_6), .b(6'b100011), .gt(comparator_2_gt), .eq(comparator_2_eq), .lt(comparator_2_lt));
  Comparator #(.width(6)) comparator_3 (
    .a(in_7), .b(6'b100011), .gt(comparator_3_gt), .eq(comparator_3_eq), .lt(comparator_3_lt));
  Comparator #(.width(6)) comparator_4 (
    .a(in_8), .b(6'b100011), .gt(comparator_4_gt), .eq(comparator_4_eq), .lt(comparator_4_lt));
  Comparator #(.width(6), .mode("unsigned")) comparator_5 (.a(adder_1_out), .b({6{1'b1}}));  // open: gt, eq, lt
  Comparator #(.width(6), .mode("unsigned")) comparator_6 (.a(adder_2_out), .b({6{1'b1}}));  // open: gt, eq, lt
  Comparator #(.width(6), .mode("unsigned")) comparator_7 (.a(subtractor_1_out), .b({6{1'b1}}));  // open: gt, eq, lt
  Comparator #(.width(6), .mode("unsigned")) comparator_8 (.a(subtractor_2_out), .b({6{1'b1}}));  // open: gt, eq, lt
endmodule
